# Fritzing sketch Controlboard (saved by Fritzing 1.0.1rc)
circuit board: 5.27236cm x 5.55907cm
breadboards: 1

parts:
  SDA_IN = Pad [width=7.902222222222222 height=9.03111111111111 connect=center]
  SCL_IN = Pad [width=7.902222222222222 height=9.03111111111111 connect=center]
  VCC = Pad [width=7.902222222222222 height=9.03111111111111 connect=center]
  GND = Pad [width=7.902222222222222 height=9.03111111111111 connect=center]
  SDA_OUT1 = Pad [width=7.902222222222222 height=9.03111111111111 connect=center]
  SCL_OUT1 = Pad [width=7.902222222222222 height=9.03111111111111 connect=center]
  VCC_2 = Pad [width=7.902222222222222 height=9.03111111111111 connect=center]
  GND_2 = Pad [width=7.902222222222222 height=9.03111111111111 connect=center]
  SDA_OUT2 = Pad [width=7.902222222222222 height=9.03111111111111 connect=center]
  SCL_OUT2 = Pad [width=7.902222222222222 height=9.03111111111111 connect=center]
  VCC_3 = Pad [width=7.902222222222222 height=9.03111111111111 connect=center]
  GND_3 = Pad [width=7.902222222222222 height=9.03111111111111 connect=center]

nets:
  N1: SDA_IN.pad, SDA_OUT1.pad, SDA_OUT2.pad
  N2: SCL_IN.pad, SCL_OUT1.pad, SCL_OUT2.pad
  N3: VCC.pad, VCC_2.pad, VCC_3.pad
  N4: GND.pad, GND_2.pad, GND_3.pad
