# Fritzing sketch Power Supply (saved by Fritzing 1.0.1rc)
circuit board: 7.78792cm x 10.0462cm
breadboards: 1

parts:
  M1 = RioRand LM2596
  M2 = RioRand LM2596
  M3 = RioRand LM2596
  Vin = Pad [width=7.902222222222222 height=9.03111111111111 connect=center]
  GND_out = Pad [width=7.902222222222222 height=9.03111111111111 connect=center]
  C1 = Capacitor [package=cap-pth-small-kit]
  C2 = Capacitor [package=cap-pth-small-kit]
  C3 = Capacitor [package=cap-pth-small-kit]
  C4 = Capacitor [package=cap-pth-small-kit]
  C5 = Capacitor [package=cap-pth-small-kit]
  Line_Vout = Pad [width=7.902222222222222 height=9.03111111111111 connect=center]
  Line_GND_In = Pad [width=7.902222222222222 height=9.03111111111111 connect=center]
  C6 = Capacitor [package=cap-pth-small-kit]
  C7 = Capacitor [package=cap-pth-small-kit]
  C8 = Capacitor [package=cap-pth-small-kit]
  3_3v_OUT = Pad [width=7.902222222222222 height=9.03111111111111 connect=center]
  3_3v_GND = Pad [width=7.902222222222222 height=9.03111111111111 connect=center]
  5v_750mA_OUT = Pad [width=7.902222222222222 height=9.03111111111111 connect=center]
  5v_750mA_GND = Pad [width=7.902222222222222 height=9.03111111111111 connect=center]
  C9 = Capacitor [package=cap-pth-small-kit]
  5v_1A_OUT = Pad [width=7.902222222222222 height=9.03111111111111 connect=center]
  5v_1A_GND = Pad [width=7.902222222222222 height=9.03111111111111 connect=center]

nets:
  N1: M1.Pin_1, M2.Pin_1, M3.Pin_1, Vin.pad, C1.1, C2.1, C3.1, C4.2, C5.2, Line_Vout.pad, C6.2
  N2: M1.Pin_2, M2.Pin_2, M3.Pin_2, GND_out.pad, C1.2, C2.2, C3.2, C4.1, C5.1, Line_GND_In.pad, C6.1
  N3: M1.Pin_3, C7.1, 3_3v_OUT.pad
  N4: M1.Pin_4, C7.2, 3_3v_GND.pad
  N5: M2.Pin_3, C8.1, 5v_750mA_OUT.pad
  N6: M2.Pin_4, C8.2, 5v_750mA_GND.pad
  N7: M3.Pin_3, C9.1, 5v_1A_OUT.pad
  N8: M3.Pin_4, C9.2, 5v_1A_GND.pad

notes:
  LM2596 - 5v - 1A
  LM2596 - 5v - 750mA
  LM2596 - 3.3v - 250mA
  v0.0.4
  Made for TAFY
